// Digital circuit ex01.dig as structural Verilog
module ex01 (
  input  clk
);

  wire add_1_s, decoder_1_out_0, decoder_1_out_1, decoder_1_out_2, decoder_1_out_3, or_1_out, R4_q;
  wire [1:0] multiplexer_1_out, R0_q, R1_q, R2_q, R3_q, undriven;

  Register R1 (.C(clk), .Q(R1_q[0]));  // open: D, en
  Register R2 (.C(clk), .Q(R2_q[0]));  // open: D, en
  Register R0 (.C(clk), .Q(R0_q[0]));  // open: D, en
  Register R3 (.C(clk), .Q(R3_q[0]));  // open: D, en
  Multiplexer #(.Selector_Bits(2), .Bits(2)) multiplexer_1 (
    .sel(undriven), .in_0(R0_q), .in_1(R1_q), .in_2(R2_q), .in_3(R3_q), .out(multiplexer_1_out));
  Decoder #(.Selector_Bits(2)) decoder_1 (
    .sel(undriven), .out_0(decoder_1_out_0), .out_1(decoder_1_out_1), .out_2(decoder_1_out_2),
    .out_3(decoder_1_out_3));
  Add add_1 (.a(R4_q), .b(multiplexer_1_out[0]), .s(add_1_s));  // open: c_i, c_o
  or or_1 (or_1_out, decoder_1_out_3, decoder_1_out_2, decoder_1_out_1, decoder_1_out_0);
  Register R4 (.D(add_1_s), .C(clk), .en(or_1_out), .Q(R4_q));
  // Pins of 1 and 2 bits meet at multiplexer_1_out
  // Pins of 1 and 2 bits meet at R0_q
  // Pins of 1 and 2 bits meet at R1_q
  // Pins of 1 and 2 bits meet at R2_q
  // Pins of 1 and 2 bits meet at R3_q

  // Notes on the sheet:
  //   T0
  //   T1
  //   T2
  //   T3
  //   MUX
  //   ENC
endmodule
