// Digital circuit ex02.dig as structural Verilog
module ex02 (
);

  wire add_1_s, and_1_out, and_2_out, comparator_1_eq, multiplexer_1_out, not_1_out, not_2_out, or_1_out,
       R1_q, R3_q, undriven, undriven_2, undriven_3, undriven_4, undriven_5, undriven_6, undriven_7;

  Comparator comparator_1 (.a(undriven_5), .b(R1_q), .eq(comparator_1_eq));  // open: gt, lt
  Register R3 (.Q(R3_q));  // open: D, C, en
  Register R2 (.D(R1_q), .en(undriven_4));  // open: C, Q
  and and_1 (and_1_out, undriven_2, undriven_4);
  not not_1 (not_1_out, comparator_1_eq);
  not not_2 (not_2_out, R3_q);
  and and_2 (and_2_out, undriven, undriven_3, comparator_1_eq);
  Decoder decoder_1 (.sel(undriven_7), .out_0(and_1_out), .out_1(not_1_out));
  Multiplexer multiplexer_1 (.sel(undriven_7), .in_0(not_2_out), .in_1(undriven_6), .out(multiplexer_1_out));
  or or_1 (or_1_out, and_1_out, and_2_out, undriven_4);
  Add add_1 (.a(R1_q), .b(multiplexer_1_out), .c_i(and_1_out), .s(add_1_s));  // open: c_o
  Register R1 (.D(add_1_s), .en(or_1_out), .Q(R1_q));  // open: C

  // Notes on the sheet:
  //   z
  //   y
  //   T1
  //   T2
  //   0
  //   1
  //   EN
  //   MX
  //   Cl
endmodule
