// Digital circuit ex03.dig as structural Verilog
module ex03 (
);

  wire and_1_out, and_2_out, and_3_out, and_4_out, and_5_out, comparator_1_eq, multiplexer_1_out, not_1_out,
       not_2_out, not_3_out, or_1_out, ramdualport_1_d, register_1_q, undriven, undriven_2, undriven_3,
       undriven_4;
  wire [1:0] R2_q;

  and and_1 (and_1_out, undriven_2, undriven_3);
  not not_1 (not_1_out, undriven_3);
  not not_2 (not_2_out, undriven_2);
  Comparator comparator_1 (.a(register_1_q), .b(R2_q[0]), .eq(comparator_1_eq));  // open: gt, lt
  Register R2 (.Q(R2_q[0]));  // open: D, C, en
  and and_2 (and_2_out, not_1_out, undriven_2);
  and and_3 (and_3_out, undriven, not_2_out);
  RAMDualPort ramdualport_1 (
    .A(R2_q), .Din(register_1_q), .str(and_2_out), .ld(and_3_out), .D(ramdualport_1_d));  // open: C
  not not_3 (not_3_out, undriven_2);
  and and_4 (and_4_out, not_3_out, undriven);
  and and_5 (and_5_out, and_1_out, comparator_1_eq);
  Multiplexer multiplexer_1 (.sel(undriven_4), .in_0(R2_q[0]), .in_1(ramdualport_1_d), .out(multiplexer_1_out));
  Decoder decoder_1 (.sel(undriven_4), .out_0(and_5_out), .out_1(and_4_out));
  Register register_1 (.D(multiplexer_1_out), .en(or_1_out), .Q(register_1_q));  // open: C
  or or_1 (or_1_out, and_1_out, and_4_out);
  // Pins of 1 and 2 bits meet at R2_q

  // Notes on the sheet:
  //   W
  //   P
  //   Q
  //   Cl
endmodule
